// Logisim project Lab_2_Solutions.circ as structural Verilog: 5 circuits, main circuit digit_counter
module digit_counter (
  input  v3,
  input  v2,
  input  v1,
  input  v0
);

  wire circuita_1_o0, circuita_1_o1, circuita_1_o2, d0, d1, d2, d3, d4, d5, d6, multiplexer_1_out,
       multiplexer_2_out, multiplexer_3_out, multiplexer_4_out, s0, s1, s2, s3, s4, s5, s6, z;
  wire [7:0] seg7_decoder_1_o_seg;

  CircuitA circuita_1 (.i2(v2), .i1(v1), .i0(v0), .o2(circuita_1_o2), .o1(circuita_1_o1), .o0(circuita_1_o0));
  comp comp_1 (.v3(v3), .v2(v2), .v1(v1), .v0(v0), .o0(z));
  Multiplexer multiplexer_1 (.in0(v3), .out(multiplexer_1_out), .sel(z));  // open: in1
  Multiplexer multiplexer_2 (.in0(v2), .in1(circuita_1_o2), .out(multiplexer_2_out), .sel(z));
  Multiplexer multiplexer_3 (.in0(v1), .in1(circuita_1_o1), .out(multiplexer_3_out), .sel(z));
  Multiplexer multiplexer_4 (.in0(v0), .in1(circuita_1_o0), .out(multiplexer_4_out), .sel(z));
  _7_Segment_Display u_7_segment_display_1 (.g(d0), .f(d1), .a(d6), .b(d5), .e(d2), .d(d3), .c(d4));  // open: dp
  _7_Segment_Display u_7_segment_display_2 (.g(s6), .f(s5), .a(s0), .b(s1), .e(s4), .d(s3), .c(s2));  // open: dp
  Seg7_Decoder seg7_decoder_1 (
    .i_m3(multiplexer_1_out), .i_m2(multiplexer_2_out), .i_m1(multiplexer_3_out), .i_m0(multiplexer_4_out),
    .o_seg(seg7_decoder_1_o_seg));
  circuitB circuitb_1 (.z(z), .s6(d0), .s5(d1), .s4(d2), .s3(d3), .s2(d4), .s1(d5), .s0(d6));
  not not_1 (s0, seg7_decoder_1_o_seg[0]);
  not not_2 (s1, seg7_decoder_1_o_seg[1]);
  not not_3 (s2, seg7_decoder_1_o_seg[2]);
  not not_4 (s3, seg7_decoder_1_o_seg[3]);
  not not_5 (s4, seg7_decoder_1_o_seg[4]);
  not not_6 (s5, seg7_decoder_1_o_seg[5]);
  not not_7 (s6, seg7_decoder_1_o_seg[6]);
endmodule

module Seg7_Decoder (
  input  i_m3,
  input  i_m2,
  input  i_m1,
  input  i_m0,
  output [7:0] o_seg
);

  wire and_1_out, and_2_out, and_3_out, and_4_out, and_5_out, and_6_out, and_7_out, and_8_out, and_10_out,
       and_11_out, and_12_out, and_13_out, not_1_out, not_2_out, not_3_out, not_4_out;

  not not_1 (not_1_out, i_m3);
  not not_2 (not_2_out, i_m2);
  not not_3 (not_3_out, i_m1);
  not not_4 (not_4_out, i_m0);
  and and_1 (and_1_out, not_1_out, not_2_out, not_3_out);
  and and_2 (and_2_out, i_m2, i_m1, i_m0);
  and and_3 (and_3_out, not_1_out, not_2_out, i_m0);
  and and_4 (and_4_out, not_2_out, i_m1);
  and and_5 (and_5_out, i_m2, not_3_out);
  and and_6 (and_6_out, not_1_out, not_2_out, not_3_out, i_m0);
  and and_7 (and_7_out, i_m2, not_3_out, not_4_out);
  and and_8 (and_8_out, i_m2, i_m1, i_m0);
  and and_9 (o_seg[2], not_2_out, i_m1, not_4_out);
  and and_10 (and_10_out, i_m2, not_3_out, i_m0);
  and and_11 (and_11_out, i_m2, i_m1, not_4_out);
  and and_12 (and_12_out, not_1_out, not_2_out, not_3_out, i_m0);
  and and_13 (and_13_out, i_m2, not_3_out, not_4_out);
  or or_1 (o_seg[6], and_1_out, and_2_out);
  or or_2 (o_seg[5], and_3_out, and_4_out);
  or or_3 (o_seg[4], i_m0, and_5_out);
  or or_4 (o_seg[3], and_6_out, and_7_out, and_8_out);
  or or_5 (o_seg[1], and_10_out, and_11_out);
  or or_6 (o_seg[0], and_12_out, and_13_out);

  assign o_seg[7] = 1'b1;
endmodule

module CircuitA (
  input  i2,
  input  i1,
  input  i0,
  output o2,
  output o1,
  output o0
);

  not not_1 (o1, i1);
  and and_1 (o2, i2, i1);

  assign o0 = i0;
endmodule

module comp (
  input  v3,
  input  v2,
  input  v1,
  input  v0,
  output o0
);

  wire and_1_out, and_2_out;

  and and_1 (and_1_out, v3, v1, v0);
  and and_2 (and_2_out, v3, v2);
  or or_1 (o0, and_1_out, and_2_out);
endmodule

module circuitB (
  input  z,
  output s6,
  output s5,
  output s4,
  output s3,
  output s2,
  output s1,
  output s0
);

  not not_1 (s0, z);

  assign s1 = 1'b1;
  assign s2 = 1'b1;
  assign s3 = s0;
  assign s4 = s0;
  assign s5 = s0;
  assign s6 = 1'b0;
endmodule
