// Logisim project lab_2_part3.circ as structural Verilog: 3 circuits, main circuit ripple_adder
module ripple_adder (
  input  ci,
  input  a0,
  input  b0,
  input  a2,
  input  b2,
  input  a1,
  input  b1,
  input  a3,
  input  b3,
  output over,
  output s0,
  output s1,
  output s2,
  output s3,
  output co
);

  wire full_adder_1_co, full_adder_2_co, full_adder_3_co;

  Full_Adder full_adder_1 (.ci(ci), .a(a0), .b(b0), .s(s0), .co(full_adder_1_co));
  Full_Adder full_adder_2 (.ci(full_adder_1_co), .a(a1), .b(b1), .s(s1), .co(full_adder_2_co));
  Full_Adder full_adder_3 (.ci(full_adder_2_co), .a(a2), .b(b2), .s(s2), .co(full_adder_3_co));
  Full_Adder full_adder_4 (.ci(full_adder_3_co), .a(a3), .b(b3), .s(s3), .co(co));
  light light_1 (.c0(co), .s0(s0), .s1(s1), .s2(s2), .s3(s3), .over(over));
endmodule

module Full_Adder (
  input  ci,
  input  a,
  input  b,
  output s,
  output co
);

  wire xor_1_out;

  xor xor_1 (xor_1_out, a, b);
  Multiplexer multiplexer_1 (.in0(b), .in1(ci), .out(co), .sel(xor_1_out));
  xor xor_2 (s, ci, xor_1_out);
endmodule

module light (
  input  c0,
  input  s0,
  input  s1,
  input  s2,
  input  s3,
  output over
);

  wire and_1_out, and_2_out;

  and and_1 (and_1_out, s0, s2, s3);
  and and_2 (and_2_out, s0, s1);
  or or_1 (over, c0, and_1_out, and_2_out);
endmodule
