// Logisim project p4_lab2.circ as structural Verilog: 3 circuits, main circuit digadder
module digadder (
  input  in_1,
  input  in_2,
  input  in_3,
  input  in_4,
  input  in_5,
  input  in_6,
  input  in_7,
  input  in_8,
  input  in_9
);

  wire d0, d1, d2, d3, d4, d5, d6, minus10_1_r0, minus10_1_r1, minus10_1_r2, minus10_1_r3, multiplexer_1_out,
       multiplexer_2_out, multiplexer_3_out, multiplexer_4_out, ripple_adder_1_co, ripple_adder_1_s0,
       ripple_adder_1_s1, ripple_adder_1_s2, ripple_adder_1_s3, s0, s1, s2, s3, s4, s5, s6, z;
  wire [7:0] seg7_decoder_1_o_seg;

  ripple_adder ripple_adder_1 (
    .ci(in_1), .a0(in_2), .b0(in_3), .a2(in_4), .b2(in_5), .a1(in_6), .b1(in_7), .a3(in_8), .b3(in_9),
    .s0(ripple_adder_1_s0), .s1(ripple_adder_1_s1), .s2(ripple_adder_1_s2), .s3(ripple_adder_1_s3),
    .co(ripple_adder_1_co));  // open: over
  minus10 minus10_1 (
    .co(ripple_adder_1_co), .s3(ripple_adder_1_s3), .s2(ripple_adder_1_s2), .s1(ripple_adder_1_s1),
    .s0(ripple_adder_1_s0), .r3(minus10_1_r3), .r2(minus10_1_r2), .r1(minus10_1_r1), .r0(minus10_1_r0));
  p4_comp p4_comp_1 (
    .co(ripple_adder_1_co), .s3(ripple_adder_1_s3), .s2(ripple_adder_1_s2), .s1(ripple_adder_1_s1), .o0(z));
  _7_Segment_Display u_7_segment_display_1 (.g(d0), .f(d1), .a(d6), .b(d5), .e(d2), .d(d3), .c(d4));  // open: dp
  Multiplexer multiplexer_1 (.in0(ripple_adder_1_s3), .in1(minus10_1_r3), .out(multiplexer_1_out), .sel(z));
  Multiplexer multiplexer_2 (.in0(ripple_adder_1_s2), .in1(minus10_1_r2), .out(multiplexer_2_out), .sel(z));
  Multiplexer multiplexer_3 (.in0(ripple_adder_1_s1), .in1(minus10_1_r1), .out(multiplexer_3_out), .sel(z));
  Multiplexer multiplexer_4 (.in0(ripple_adder_1_s0), .in1(minus10_1_r0), .out(multiplexer_4_out), .sel(z));
  _7_Segment_Display u_7_segment_display_2 (.g(s6), .f(s5), .a(s0), .b(s1), .e(s4), .d(s3), .c(s2));  // open: dp
  circuitB circuitb_1 (.z(z), .s6(d0), .s5(d1), .s4(d2), .s3(d3), .s2(d4), .s1(d5), .s0(d6));
  Seg7_Decoder seg7_decoder_1 (
    .i_m3(multiplexer_1_out), .i_m2(multiplexer_2_out), .i_m1(multiplexer_3_out), .i_m0(multiplexer_4_out),
    .o_seg(seg7_decoder_1_o_seg));
  not not_1 (s0, seg7_decoder_1_o_seg[0]);
  not not_2 (s1, seg7_decoder_1_o_seg[1]);
  not not_3 (s2, seg7_decoder_1_o_seg[2]);
  not not_4 (s3, seg7_decoder_1_o_seg[3]);
  not not_5 (s4, seg7_decoder_1_o_seg[4]);
  not not_6 (s5, seg7_decoder_1_o_seg[5]);
  not not_7 (s6, seg7_decoder_1_o_seg[6]);
endmodule

module p4_comp (
  input  co,
  input  s3,
  input  s2,
  input  s1,
  output o0
);

  wire and_1_out, and_2_out;

  and and_1 (and_1_out, s3, s1);
  and and_2 (and_2_out, s3, s2);
  or or_1 (o0, and_1_out, and_2_out, co);
endmodule

module minus10 (
  input  co,
  input  s3,
  input  s2,
  input  s1,
  input  s0,
  output r3,
  output r2,
  output r1,
  output r0
);

  wire and_2_out, and_3_out, not_1_out;

  not not_1 (not_1_out, s3);
  not not_2 (r1, s1);
  and and_1 (r3, not_1_out, s1);
  and and_2 (and_2_out, s2, s1);
  and and_3 (and_3_out, not_1_out, r1);
  or or_1 (r2, and_2_out, and_3_out);

  assign r0 = s0;
endmodule
