// Logisim project p5_lab2.circ as structural Verilog: 2 circuits, main circuit patvadder
module patvadder (
  input  ci,
  input  a0,
  input  b0,
  input  a2,
  input  b2,
  input  a1,
  input  b1,
  input  a3,
  input  b3,
  output co,
  output s3,
  output s2,
  output s1,
  output s0
);

  wire minus10_1_r0, minus10_1_r1, minus10_1_r2, minus10_1_r3, ripple_adder_1_co, ripple_adder_1_s0,
       ripple_adder_1_s1, ripple_adder_1_s2, ripple_adder_1_s3;

  ripple_adder ripple_adder_1 (
    .ci(ci), .a0(a0), .b0(b0), .a2(a2), .b2(b2), .a1(a1), .b1(b1), .a3(a3), .b3(b3), .s0(ripple_adder_1_s0),
    .s1(ripple_adder_1_s1), .s2(ripple_adder_1_s2), .s3(ripple_adder_1_s3), .co(ripple_adder_1_co));  // open: over
  minus10 minus10_1 (
    .co(ripple_adder_1_co), .s3(ripple_adder_1_s3), .s2(ripple_adder_1_s2), .s1(ripple_adder_1_s1),
    .s0(ripple_adder_1_s0), .r3(minus10_1_r3), .r2(minus10_1_r2), .r1(minus10_1_r1), .r0(minus10_1_r0));
  p4_comp p4_comp_1 (
    .co(ripple_adder_1_co), .s3(ripple_adder_1_s3), .s2(ripple_adder_1_s2), .s1(ripple_adder_1_s1), .o0(co));
  Multiplexer multiplexer_1 (.in0(ripple_adder_1_s3), .in1(minus10_1_r3), .out(s3), .sel(co));
  Multiplexer multiplexer_2 (.in0(ripple_adder_1_s2), .in1(minus10_1_r2), .out(s2), .sel(co));
  Multiplexer multiplexer_3 (.in0(ripple_adder_1_s1), .in1(minus10_1_r1), .out(s1), .sel(co));
  Multiplexer multiplexer_4 (.in0(ripple_adder_1_s0), .in1(minus10_1_r0), .out(s0), .sel(co));

  // Other names for the same wires on the sheet: z = co
endmodule

module main (
  input  in_1,
  input  in_2,
  input  in_3,
  input  in_4,
  input  in_5,
  input  in_6,
  input  in_7,
  input  in_8,
  input  in_9,
  input  in_10,
  input  in_11,
  input  in_12,
  input  in_13,
  input  in_14,
  input  in_15,
  input  in_16,
  input  in_17
);

  wire d0, d1, d2, d3, d4, d5, d6, patvadder_1_co, patvadder_1_s0, patvadder_1_s1, patvadder_1_s2,
       patvadder_1_s3, patvadder_2_co, patvadder_2_s0, patvadder_2_s1, patvadder_2_s2, patvadder_2_s3, s0,
       s1, s2, s3, s4, s5, s6;
  wire [7:0] seg7_decoder_1_o_seg, seg7_decoder_2_o_seg;

  patvadder patvadder_1 (
    .ci(in_1), .a0(in_2), .b0(in_4), .a2(in_6), .b2(in_8), .a1(in_10), .b1(in_12), .a3(in_14), .b3(in_16),
    .co(patvadder_1_co), .s3(patvadder_1_s3), .s2(patvadder_1_s2), .s1(patvadder_1_s1), .s0(patvadder_1_s0));
  Seg7_Decoder seg7_decoder_1 (
    .i_m3(patvadder_1_s3), .i_m2(patvadder_1_s2), .i_m1(patvadder_1_s1), .i_m0(patvadder_1_s0),
    .o_seg(seg7_decoder_1_o_seg));
  not not_1 (s0, seg7_decoder_1_o_seg[0]);
  not not_2 (s1, seg7_decoder_1_o_seg[1]);
  not not_3 (s2, seg7_decoder_1_o_seg[2]);
  not not_4 (s3, seg7_decoder_1_o_seg[3]);
  not not_5 (s4, seg7_decoder_1_o_seg[4]);
  not not_6 (s5, seg7_decoder_1_o_seg[5]);
  not not_7 (s6, seg7_decoder_1_o_seg[6]);
  patvadder patvadder_2 (
    .ci(patvadder_1_co), .a0(in_3), .b0(in_5), .a2(in_7), .b2(in_9), .a1(in_11), .b1(in_13), .a3(in_15),
    .b3(in_17), .co(patvadder_2_co), .s3(patvadder_2_s3), .s2(patvadder_2_s2), .s1(patvadder_2_s1),
    .s0(patvadder_2_s0));
  _7_Segment_Display u_7_segment_display_1 (.b(patvadder_2_co), .c(patvadder_2_co));  // open: g, f, a, e, d, dp
  _7_Segment_Display u_7_segment_display_2 (.g(d6), .f(d5), .a(d0), .b(d1), .e(d4), .d(d3), .c(d2));  // open: dp
  Seg7_Decoder seg7_decoder_2 (
    .i_m3(patvadder_2_s3), .i_m2(patvadder_2_s2), .i_m1(patvadder_2_s1), .i_m0(patvadder_2_s0),
    .o_seg(seg7_decoder_2_o_seg));
  not not_8 (d0, seg7_decoder_2_o_seg[0]);
  not not_9 (d1, seg7_decoder_2_o_seg[1]);
  not not_10 (d2, seg7_decoder_2_o_seg[2]);
  not not_11 (d3, seg7_decoder_2_o_seg[3]);
  not not_12 (d4, seg7_decoder_2_o_seg[4]);
  not not_13 (d5, seg7_decoder_2_o_seg[5]);
  not not_14 (d6, seg7_decoder_2_o_seg[6]);
  _7_Segment_Display u_7_segment_display_3 (.g(s6), .f(s5), .a(s0), .b(s1), .e(s4), .d(s3), .c(s2));  // open: dp
endmodule
