// Logisim project lab3.circ as structural Verilog: 4 circuits, main circuit main
module main (
  input  d0,
  input  d1,
  input  d2,
  input  d3,
  input  d4,
  input  d5,
  input  d6,
  input  d7,
  input  clk,
  input  rst
);

  wire d0_t, d1_t, d2_t, d3_t, d4_t, d5_t, d6_t, f0, f1, f2, f3, f4, f5, f6, g0, g1, g2, g3, g4, g5, g6, s0,
       s1, s2, s3, s4, s5, s6;
  wire [7:0] register_1_q, seg7_decoder_1_o_seg, seg7_decoder_2_o_seg, seg7_decoder_3_o_seg,
       seg7_decoder_4_o_seg;

  Register register_1 (.D({d7, d6, d5, d4, d3, d2, d1, d0}), .clk(clk), .Q(register_1_q), .clr(rst));  // open: en
  Seg7_Decoder seg7_decoder_1 (
    .i_m3(register_1_q[3]), .i_m2(register_1_q[2]), .i_m1(register_1_q[1]), .i_m0(register_1_q[0]),
    .o_seg(seg7_decoder_1_o_seg));
  Seg7_Decoder seg7_decoder_2 (
    .i_m3(register_1_q[7]), .i_m2(register_1_q[6]), .i_m1(register_1_q[5]), .i_m0(register_1_q[4]),
    .o_seg(seg7_decoder_2_o_seg));
  Seg7_Decoder seg7_decoder_3 (.i_m3(d3), .i_m2(d2), .i_m1(d1), .i_m0(d0), .o_seg(seg7_decoder_3_o_seg));
  Seg7_Decoder seg7_decoder_4 (.i_m3(d7), .i_m2(d6), .i_m1(d5), .i_m0(d4), .o_seg(seg7_decoder_4_o_seg));
  not not_1 (s0, seg7_decoder_1_o_seg[0]);
  not not_2 (s1, seg7_decoder_1_o_seg[1]);
  not not_3 (s2, seg7_decoder_1_o_seg[2]);
  not not_4 (s3, seg7_decoder_1_o_seg[3]);
  not not_5 (s4, seg7_decoder_1_o_seg[4]);
  not not_6 (s5, seg7_decoder_1_o_seg[5]);
  not not_7 (s6, seg7_decoder_1_o_seg[6]);
  not not_8 (d0_t, seg7_decoder_2_o_seg[0]);
  not not_9 (d1_t, seg7_decoder_2_o_seg[1]);
  not not_10 (d2_t, seg7_decoder_2_o_seg[2]);
  not not_11 (d3_t, seg7_decoder_2_o_seg[3]);
  not not_12 (d4_t, seg7_decoder_2_o_seg[4]);
  not not_13 (d5_t, seg7_decoder_2_o_seg[5]);
  not not_14 (d6_t, seg7_decoder_2_o_seg[6]);
  not not_15 (f0, seg7_decoder_3_o_seg[0]);
  not not_16 (f1, seg7_decoder_3_o_seg[1]);
  not not_17 (f2, seg7_decoder_3_o_seg[2]);
  not not_18 (f3, seg7_decoder_3_o_seg[3]);
  not not_19 (f4, seg7_decoder_3_o_seg[4]);
  not not_20 (f5, seg7_decoder_3_o_seg[5]);
  not not_21 (f6, seg7_decoder_3_o_seg[6]);
  not not_22 (g0, seg7_decoder_4_o_seg[0]);
  not not_23 (g1, seg7_decoder_4_o_seg[1]);
  not not_24 (g2, seg7_decoder_4_o_seg[2]);
  not not_25 (g3, seg7_decoder_4_o_seg[3]);
  not not_26 (g4, seg7_decoder_4_o_seg[4]);
  not not_27 (g5, seg7_decoder_4_o_seg[5]);
  not not_28 (g6, seg7_decoder_4_o_seg[6]);
  _7_Segment_Display u_7_segment_display_1 (.g(s6), .f(s5), .a(s0), .b(s1), .e(s4), .d(s3), .c(s2));  // open: dp
  _7_Segment_Display u_7_segment_display_2 (
    .g(d6_t), .f(d5_t), .a(d0_t), .b(d1_t), .e(d4_t), .d(d3_t), .c(d2_t));  // open: dp
  _7_Segment_Display u_7_segment_display_3 (.g(f6), .f(f5), .a(f0), .b(f1), .e(f4), .d(f3), .c(f2));  // open: dp
  _7_Segment_Display u_7_segment_display_4 (.g(g6), .f(g5), .a(g0), .b(g1), .e(g4), .d(g3), .c(g2));  // open: dp
endmodule

module DFF (
  input  D,
  input  Clk,
  output Qa,
  output Qb
);

  wire nand_1_out, nand_2_out, not_1_out;

  not not_1 (not_1_out, D);
  nand nand_1 (nand_1_out, D, Clk);
  nand nand_2 (nand_2_out, Clk, not_1_out);
  nand nand_3 (Qa, nand_1_out, Qb);
  nand nand_4 (Qb, Qa, nand_2_out);
endmodule

module MS (
  input  D,
  input  Clk,
  output Qa,
  output Qb
);

  wire dff_1_qa, not_1_out;

  not not_1 (not_1_out, Clk);
  DFF dff_1 (.D(D), .Clk(not_1_out), .Qa(dff_1_qa));  // open: Qb
  DFF dff_2 (.D(dff_1_qa), .Clk(Clk), .Qa(Qa), .Qb(Qb));
endmodule

module part4 (
  input  D,
  output Qa,
  output Qa_not,
  output Qb,
  output Qb_not,
  output Qc,
  output Qc_not
);

  wire Clk_out, not_1_out;

  Clock Clk (.out(Clk_out));
  not not_1 (not_1_out, Clk_out);
  DFF dff_1 (.D(D), .Clk(Clk_out), .Qa(Qa), .Qb(Qa_not));
  MS ms_1 (.D(D), .Clk(Clk_out), .Qa(Qb), .Qb(Qb_not));
  MS ms_2 (.D(D), .Clk(not_1_out), .Qa(Qc), .Qb(Qc_not));
endmodule
