// Logisim project T_counter.circ as structural Verilog: 1 circuit, main circuit main
module main (
  input  enable,
  input  Clear
);

  wire and_1_out, and_2_out, and_3_out, clk_out, t_ff_1_q, t_ff_2_q, t_ff_3_q;

  Clock clk (.out(clk_out));
  T_Flip_Flop t_ff_1 (.T(enable), .clk(clk_out), .Q(t_ff_1_q), .reset(Clear));  // open: Qn, preset
  and and_1 (and_1_out, enable, t_ff_1_q);
  T_Flip_Flop t_ff_2 (.T(and_1_out), .clk(clk_out), .Q(t_ff_2_q), .reset(Clear));  // open: Qn, preset
  and and_2 (and_2_out, and_1_out, t_ff_2_q);
  T_Flip_Flop t_ff_3 (.T(and_2_out), .clk(clk_out), .Q(t_ff_3_q), .reset(Clear));  // open: Qn, preset
  and and_3 (and_3_out, and_2_out, t_ff_3_q);
  T_Flip_Flop t_ff_4 (.T(and_3_out), .clk(clk_out), .reset(Clear));  // open: Q, Qn, preset

  // Notes on the sheet:
  //   LSB
  //   MSB
endmodule
